// Logisim project alu.circ as structural Verilog: 3 circuits, main circuit main
module main (
  input  [15:0] X,
  input  [15:0] Y,
  input  [3:0] switch__S,
  output signed_overflow,
  output [15:0] result,
  output equal
);

  wire addoverflow_1_out, comparator_1_lt, subtractoverflow_1_out;
  wire [15:0] adder_1_out, and_1_out, multiplexer_1_out, or_1_out, shifter_1_out, shifter_2_out,
       shifter_3_out, subtractor_1_out;

  assign and_1_out = X & Y;  // AND_Gate and_1, 16 bits wide
  assign or_1_out = X | Y;  // OR_Gate or_1, 16 bits wide
  Comparator #(.width(16)) comparator_1 (.a(X), .b(Y), .lt(comparator_1_lt));  // open: gt, eq
  Shifter #(.width(16)) shifter_1 (.in(X), .\dist (Y[3:0]), .out(shifter_1_out));
  Shifter #(.width(16), .shift("lr")) shifter_2 (.in(X), .\dist (Y[3:0]), .out(shifter_2_out));
  Shifter #(.width(16), .shift("ar")) shifter_3 (.in(X), .\dist (Y[3:0]), .out(shifter_3_out));
  Adder #(.width(16)) adder_1 (.a(X), .b(Y), .out(adder_1_out));  // open: cin, cout
  Subtractor #(.width(16)) subtractor_1 (.a(X), .b(Y), .out(subtractor_1_out));  // open: bin, bout
  Multiplexer #(.width(16)) multiplexer_1 (
    .in0({16{1'b0}}), .in1(16'h1), .out(multiplexer_1_out), .sel(comparator_1_lt));  // open: en
  Multiplexer #(.select(4), .width(16)) multiplexer_2 (
    .in0(and_1_out), .in1(or_1_out), .in2(multiplexer_1_out), .in3(shifter_1_out), .in4(shifter_2_out),
    .in5(shifter_3_out), .in6(adder_1_out), .in7(subtractor_1_out), .out(result), .sel(switch__S));  // open: in8, in9, in10, in11, in12, in13, in14, in15, en
  AddOverflow addoverflow_1 (.in_1(X), .in_2(Y), .out(addoverflow_1_out));
  SubtractOverflow subtractoverflow_1 (.in_1(X), .in_2(Y), .out(subtractoverflow_1_out));
  Multiplexer #(.select(4)) multiplexer_3 (
    .in6(addoverflow_1_out), .in7(subtractoverflow_1_out), .out(signed_overflow), .sel(switch__S));  // open: in0, in1, in2, in3, in4, in5, in8, in9, in10, in11, in12, in13, in14, in15, en
  Comparator #(.width(16)) comparator_2 (.a(X), .b(Y), .eq(equal));  // open: gt, lt

  // Notes on the sheet:
  //   These are INPUTS to your circuit
  //   This is an INPUT to your circuit
  //   DO NOT CHANGE THE LOCATIONS OF THE INPUTS/OUTPUTS! IF YOU DO SO, YOU NEED TO MAKE SURE THE PINS ARE AT THE RIGHT PLACE!
  //   These are OUTPUTS to your circuit
endmodule

module AddOverflow (
  input  [15:0] in_1,
  input  [15:0] in_2,
  output out
);

  wire and_1_out, and_2_out, not_1_out, not_2_out, not_3_out;
  wire [15:0] adder_1_out;

  not not_1 (not_1_out, in_1[15]);
  Adder #(.width(16)) adder_1 (.a(in_1), .b(in_2), .out(adder_1_out));  // open: cin, cout
  not not_2 (not_2_out, in_2[15]);
  not not_3 (not_3_out, adder_1_out[15]);
  and and_1 (and_1_out, not_1_out, adder_1_out[15], not_2_out);
  and and_2 (and_2_out, in_1[15], not_3_out, in_2[15]);
  or or_1 (out, and_1_out, and_2_out);

  // Notes on the sheet:
  //   X
  //   Y
endmodule

module SubtractOverflow (
  input  [15:0] in_1,
  input  [15:0] in_2,
  output out
);

  wire and_1_out, and_2_out, not_1_out, not_2_out, not_3_out;
  wire [15:0] subtractor_1_out;

  // Probe on subtractor_1_out
  not not_1 (not_1_out, in_1[15]);
  Subtractor #(.width(16)) subtractor_1 (.a(in_1), .b(in_2), .out(subtractor_1_out));  // open: bin, bout
  not not_2 (not_2_out, subtractor_1_out[15]);
  not not_3 (not_3_out, in_2[15]);
  and and_1 (and_1_out, not_1_out, subtractor_1_out[15], in_2[15]);
  and and_2 (and_2_out, in_1[15], not_2_out, not_3_out);
  or or_1 (out, and_1_out, and_2_out);

  // Notes on the sheet:
  //   X
  //   Y
endmodule
