// Logisim project Regfile.circ as structural Verilog: 1 circuit, main circuit main
module main (
  input  [1:0] Read_register_1,
  input  [1:0] Read_register_2,
  input  [1:0] write_register,
  input  [15:0] write_data,
  input  RegWrite,
  input  clock,
  output [15:0] Reg_0_Value,
  output [15:0] Reg_1_Value,
  output [15:0] Reg_2_Value,
  output [15:0] Reg_3_Value,
  output [15:0] Read_Data_1,
  output [15:0] Read_Data_2
);

  wire demultiplexer_2_out0, demultiplexer_2_out1, demultiplexer_2_out2, demultiplexer_2_out3, or_1_out,
       or_2_out, or_3_out, or_4_out;
  wire [15:0] Write_1, Write_2, Write_3, Write_4;

  or or_1 (or_1_out, 1'b0, demultiplexer_2_out0);
  Demultiplexer #(.select(2), .width(16)) demultiplexer_1 (
    .out0(Write_1), .out1(Write_2), .out2(Write_3), .out3(Write_4), .in(write_data), .sel(write_register),
    .en(RegWrite));
  Register #(.width(16)) register_1 (.D(Write_1), .en(or_1_out), .Q(Reg_0_Value), .clk(clock));  // open: clr
  Register #(.width(16)) register_2 (.D(Write_2), .en(or_2_out), .Q(Reg_1_Value), .clk(clock));  // open: clr
  or or_2 (or_2_out, 1'b0, demultiplexer_2_out1);
  Demultiplexer #(.select(2)) demultiplexer_2 (
    .out0(demultiplexer_2_out0), .out1(demultiplexer_2_out1), .out2(demultiplexer_2_out2),
    .out3(demultiplexer_2_out3), .in(1'b1), .sel(write_register));  // open: en
  or or_3 (or_3_out, 1'b0, demultiplexer_2_out2);
  Register #(.width(16)) register_3 (.D(Write_3), .en(or_3_out), .Q(Reg_2_Value), .clk(clock));  // open: clr
  or or_4 (or_4_out, 1'b0, demultiplexer_2_out3);
  Register #(.width(16)) register_4 (.D(Write_4), .en(or_4_out), .Q(Reg_3_Value), .clk(clock));  // open: clr
  Multiplexer #(.select(2), .width(16)) multiplexer_1 (
    .in0(Reg_0_Value), .in1(Reg_1_Value), .in2(Reg_2_Value), .in3(Reg_3_Value), .out(Read_Data_1),
    .sel(Read_register_1));  // open: en
  Multiplexer #(.select(2), .width(16)) multiplexer_2 (
    .in0(Reg_0_Value), .in1(Reg_1_Value), .in2(Reg_2_Value), .in3(Reg_3_Value), .out(Read_Data_2),
    .sel(Read_register_2));  // open: en

  // Other names for the same wires on the sheet: Read_1[1:0] = Read_register_1; Read_2[1:0] = Read_register_2;
  //   Reg_0[15:0] = Reg_0_Value; Reg_1[15:0] = Reg_1_Value; Reg_2[15:0] = Reg_2_Value; Reg_3[15:0] = Reg_3_Value;
  //   Write_Reg[1:0] = write_register

  // Notes on the sheet:
  //   These are INPUTS to the circuit
  //   These are INPUTS to the circuit
  //   DO NOT CHANGE THE LOCATIONS OF THE INPUTS/OUTPUTS! IF YOU DO SO, YOU NEED TO MAKE SURE THE PINS ARE AT THE RIGHT PLACE!
  //   These are OUTPUTS to the circuit
  //   Yet again, the clock is not an actual clock, but an input, one that will should/will be inputed from the higher circuit
  //   These are OUTPUTS to the circuit
endmodule
